# Fritzing sketch print_PCB_GMR_AAL024-10E_Arduino (saved by Fritzing 0.9.3b)
circuit board: 7.1515cm x 5.5592cm

parts:
  Part1 = Adafruit ADS1115 16Bit I2C ADC [part_number="Adafruit #1085"]
  R1 = Resistor [tolerance=±5% resistance=47 package=THT]
  R2 = Resistor [tolerance=±5% resistance=2.2 package=THT]
  U1 = LM 358 Dual Op-Amp [package="DIP8 [THT]"]
  R4 = Resistor [tolerance=±5% resistance=1k package=THT]
  R5 = Resistor [tolerance=±5% resistance=10k package=THT]
  R6 = Resistor [tolerance=±5% resistance=10k package=THT]
  C2 = Ceramic Capacitor [capacitance="100 nF" voltage=16V package="100 mil [THT, multilayer]"]
  R3 = Resistor [tolerance=±5% resistance=47 package=THT]
  J1 = female pin header, 4 pins [form="♀ (female)"]
  Part2 = Arduino Uno (Rev3) - ICSP
  U2 = LM 358 Dual Op-Amp [package="DIP8 [THT]"]
  J2 = female pin header, 4 pins [form="♀ (female)"]
  R7 = Resistor [tolerance=±5% resistance=47 package=THT]
  R8 = Resistor [tolerance=±5% resistance=47 package=THT]
  R9 = Resistor [tolerance=±5% resistance=47 package=THT]
  R10 = Resistor [tolerance=±5% resistance=10k package=THT]
  R11 = Resistor [tolerance=±5% resistance=10k package=THT]
  Part3 = Adafruit ADS1115 16Bit I2C ADC [part_number="Adafruit #1085"]
  C3 = Ceramic Capacitor [capacitance="100 nF" voltage=16V package="100 mil [THT, multilayer]"]

nets:
  N1: Part1.AIN0, R6.Pin_1, C2.1, Part3.SDA
  N2: Part1.SDA, Part2.A4/SDA, Part3.AIN0
  N3: Part1.SCL, Part2.A5/SCL, Part3.AIN1
  GND: Part1.GND, R2.Pin_1, U1.connector3, C2.0, J1.pin4, Part2.GND, U2.connector4, J2.pin4, Part3.AIN2, C3.1
  VDD: Part1.VDD, U1.connector7, J1.pin1, Part2.3V3, U2.connector0, J2.pin1, Part3.AIN3
  N4: R1.Pin_0, J1.pin2, J2.pin2, R9.Pin_0
  N5: R1.Pin_1, R2.Pin_0, U1.connector2, U2.connector5, R9.Pin_1
  N6: U1.connector0, R4.Pin_1, R5.Pin_1, U2.connector7, R8.Pin_1
  N7: U1.connector1, R4.Pin_0, R3.Pin_1, U2.connector6, R7.Pin_1, R8.Pin_0
  N8: R5.Pin_0, R6.Pin_0
  N9: R3.Pin_0, J1.pin3, J2.pin3, R7.Pin_0
  N10: R10.Pin_0, R11.Pin_0
  N11: R11.Pin_1, C3.0

custom parts:
  Adafruit ADS1115 16Bit I2C ADC: For microcontrollers without an analog-to-digital converter or when you want a higher-precision ADC, the ADS1115 provides 16-bit precision at 860 samples/second over I2C. The chip can be configured as 4 single-ended input channels, or two differential channels. As a nice bonus, it even includes a programmable gain amplifier, up to x16, to help boost up smaller single/differential signals to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
